# Fritzing sketch turbina (saved by Fritzing 0.9.6b)
breadboards: 1

parts:
  U1 = TLP621 [package=THT]
  U2 = TRIAC [package=to-92]
  R1 = Resistor [tolerance=±5% power=0.25 resistance=220 package=THT]
  C1 = Film/Foil Capacitor [capacitance=100nF voltage=35V package="22.5mm [THT, pp]"]
  Z1 = Zener Diode [part_number=9.1V breakdown_voltage=9.1V package="300 mil [THT]"]
  Relé_24V = DS2Y-5-DC5V [part_number=DS2Y-5-DC5V]
  V1 = AC Power [voltage=5 frequency=60]
  D2 = Rectifier Diode [package="Melf DO-213 AA [SMD]"]
  D3 = Rectifier Diode [package="Melf DO-213 AA [SMD]"]
  D4 = Rectifier Diode [package="Melf DO-213 AA [SMD]"]
  D5 = Rectifier Diode [package="Melf DO-213 AA [SMD]"]
  Motor_Turbina = DC Motor
  C2 = Film/Foil Capacitor [capacitance=100nF voltage=35V package="22.5mm [THT, pp]"]
  D7 = Rectifier Diode [package="Melf DO-213 AA [SMD]"]
  D8 = Rectifier Diode [package="Melf DO-213 AA [SMD]"]
  C3 = Electrolytic Capacitor [capacitance=47µF voltage=100V package="100 mil [THT, electrolytic]"]

nets:
  N1: U1.Pin_4, R1.Pin_0
  N2: U1.Pin_3, Z1.anode, D8.anode, C3.+
  N3: U2.M1, Relé_24V.4_COM, V1.V+, D7.cathode
  N4: U2.G, R1.Pin_1
  N5: U2.M2, C1.+
  N6: C1.-, D2.anode, D3.cathode
  N7: Z1.cathode, C3.-
  N8: Relé_24V.8_N.O., Motor_Turbina.pin_1
  N9: Relé_24V.1_+, D2.cathode, D4.cathode
  N10: Relé_24V.16_-, D3.anode, D5.anode
  N11: Relé_24V.13_COM, V1.V-, D4.anode, D5.cathode, C2.+
  N12: Relé_24V.9_N.O., Motor_Turbina.pin_2
  N13: C2.-, D7.anode, D8.cathode
